# Fritzing sketch naventure_PCB (saved by Fritzing 0.9.3b)
circuit board: 6.48089cm x 2.97852cm

parts:
  snap = Momentary Switch [package=ksa_sealed_tac_switch]
  connex = LED - 5mm [color="Blue (505nm)" package="5 mm [THT]"]
  status = LED - 5mm [color="Green (565nm)" package="5 mm [THT]"]
  R1 = Resistor [tolerance=±5% resistance=10k package=THT]
  R2 = Resistor [tolerance=±5% resistance=10k package=THT]
  upload = Momentary Switch [package=ksa_sealed_tac_switch]
  MCU1 = Raspberry Pi Zero

nets:
  N1: snap.2, MCU1.pin_7
  N2: snap.4, connex.cathode, status.cathode, upload.3, MCU1.pin_6, MCU1.pin_9, MCU1.pin_14, MCU1.pin_25, MCU1.pin_39
  N3: connex.anode, R1.Pin_1
  N4: status.anode, R2.Pin_1
  N5: R1.Pin_0, MCU1.pin_11
  N6: R2.Pin_0, MCU1.pin_13
  N7: upload.1, MCU1.pin_5

notes:
  L@Bx
